// Logisim project TallerLogicaCombinatorios.circ as structural Verilog: 14 circuits, main circuit sumador_simple
module sumador_simple (
  input  A,
  input  B,
  output C,
  output out_4
);

  and and_1 (C, B, A);
  xor xor_1 (out_4, A, B);

  // Notes on the sheet:
  //   S
endmodule

module sumador_completo (
  input  A,
  input  B,
  input  Cin,
  output S,
  output Cout
);

  wire and_1_out, and_2_out, xor_1_out;

  and and_1 (and_1_out, B, A);
  xor xor_1 (xor_1_out, A, B);
  and and_2 (and_2_out, Cin, xor_1_out);
  xor xor_2 (S, xor_1_out, Cin);
  or or_1 (Cout, and_2_out, and_1_out);
endmodule

module sumador_4 (
  input  [3:0] A,
  input  Cin,
  input  [3:0] B,
  output [3:0] S,
  output Cout
);

  wire sumador_completo_1_cout, sumador_completo_2_cout, sumador_completo_3_cout;

  sumador_completo sumador_completo_1 (.A(A[0]), .B(B[0]), .Cin(Cin), .S(S[0]), .Cout(sumador_completo_1_cout));
  sumador_completo sumador_completo_2 (
    .A(A[1]), .B(B[1]), .Cin(sumador_completo_1_cout), .S(S[1]), .Cout(sumador_completo_2_cout));
  sumador_completo sumador_completo_3 (
    .A(A[2]), .B(B[2]), .Cin(sumador_completo_2_cout), .S(S[2]), .Cout(sumador_completo_3_cout));
  sumador_completo sumador_completo_4 (.A(A[3]), .B(B[3]), .Cin(sumador_completo_3_cout), .S(S[3]), .Cout(Cout));
  Hex_Digit_Display hex_digit_display_1 (.value(S));  // open: dp
endmodule

module comparador_cero (
  input  [3:0] A,
  output Z
);

  wire and_1_out, and_2_out, not_1_out, not_2_out, not_3_out, not_4_out;

  not not_1 (not_1_out, A[0]);
  not not_2 (not_2_out, A[1]);
  not not_3 (not_3_out, A[2]);
  not not_4 (not_4_out, A[3]);
  and and_1 (and_1_out, not_1_out, not_2_out);
  and and_2 (and_2_out, not_3_out, not_4_out);
  and and_3 (Z, and_1_out, and_2_out);
endmodule

module sumador_flags (
  input  Cin,
  input  [3:0] A,
  input  [3:0] B,
  output [3:0] S,
  output N,
  output Z,
  output V,
  output C
);

  wire and_1_out, and_2_out, and_3_out, and_4_out, not_1_out, not_2_out, not_3_out;

  not not_1 (not_1_out, A[3]);
  not not_2 (not_2_out, B[3]);
  and and_1 (and_1_out, not_1_out, not_2_out);
  and and_2 (and_2_out, A[3], B[3]);
  sumador_4 sumador_4_1 (.A(A), .Cin(Cin), .B(B), .S({N, S[2:0]}), .Cout(C));
  not not_3 (not_3_out, N);
  Hex_Digit_Display hex_digit_display_1 (.value({N, S[2:0]}));  // open: dp
  comparador_cero comparador_cero_1 (.A({N, S[2:0]}), .Z(Z));
  and and_3 (and_3_out, N, and_1_out);
  and and_4 (and_4_out, not_3_out, and_2_out);
  or or_1 (V, and_3_out, and_4_out);

  assign S[3] = N;
endmodule

module incrementador_4 (
  input  [3:0] A,
  output [3:0] S
);

  wire and_1_out, not_1_out, not_2_out, not_3_out, not_4_out;
  wire [3:0] not_5_out;

  not not_1 (not_1_out, A[0]);
  not not_2 (not_2_out, A[1]);
  not not_3 (not_3_out, A[2]);
  not not_4 (not_4_out, A[3]);
  and and_1 (and_1_out, not_1_out, A[0]);
  not not_5 (not_5_out[0], and_1_out);
  and and_2 (not_5_out[1], not_2_out, A[1]);
  and and_3 (not_5_out[2], not_3_out, A[2]);
  and and_4 (not_5_out[3], not_4_out, A[3]);
  sumador_4 sumador_4_1 (.A(A), .B(not_5_out), .S(S));  // open: Cin, Cout
  Hex_Digit_Display hex_digit_display_1 (.value(S));  // open: dp
endmodule

module inversor_4 (
  input  [3:0] A,
  input  INV,
  output [3:0] S
);

  wire not_5_out;
  wire [3:0] incrementador_4_1_s, not_1_out, onoff_1_out_3, onoff_2_out_3;

  Hex_Digit_Display hex_digit_display_1 (.value(A));  // open: dp
  not not_1 (not_1_out[0], A[0]);
  not not_2 (not_1_out[1], A[1]);
  not not_3 (not_1_out[2], A[2]);
  not not_4 (not_1_out[3], A[3]);
  not not_5 (not_5_out, INV);
  incrementador_4 incrementador_4_1 (.A(not_1_out), .S(incrementador_4_1_s));
  OnOff onoff_1 (.A(A), .in_2(not_5_out), .out_3(onoff_1_out_3));
  OnOff onoff_2 (.A(incrementador_4_1_s), .in_2(INV), .out_3(onoff_2_out_3));
  sumador_4 sumador_4_1 (.A(onoff_2_out_3), .B(onoff_1_out_3), .S(S));  // open: Cin, Cout
  Hex_Digit_Display hex_digit_display_2 (.value(S));  // open: dp
endmodule

module ALU (
  input  [3:0] A,
  input  [3:0] B,
  input  [1:0] OP,
  output N,
  output Z,
  output V,
  output C,
  output [3:0] S
);

  wire and_1_out, and_2_out, and_3_out, and_4_out, and_5_out, and_6_out, not_1_out, not_2_out, not_3_out,
       not_4_out, not_5_out, not_6_out, sumador_flags_1_c, sumador_flags_1_v, sumador_flags_2_c,
       sumador_flags_2_v;
  wire [3:0] and4bits_1_s, inversor_4_1_s, onoff_1_out_3, onoff_2_out_3, onoff_3_out_3, onoff_4_out_3,
       onoff_5_out_3, onoff_6_out_3, onoff_7_out_3, onoff_8_out_3, or4bits_1_s, sumador_flags_1_s,
       sumador_flags_2_s;

  not not_1 (not_1_out, OP[0]);
  not not_2 (not_2_out, OP[1]);
  not not_3 (not_3_out, OP[0]);
  not not_4 (not_4_out, OP[1]);
  and and_1 (and_1_out, OP[0], OP[1]);
  and and_2 (and_2_out, not_1_out, OP[1]);
  and and_3 (and_3_out, OP[0], not_2_out);
  and and_4 (and_4_out, not_3_out, not_4_out);
  OnOff onoff_1 (.A(A), .in_2(and_2_out), .out_3(onoff_1_out_3));
  OnOff onoff_2 (.A(B), .in_2(and_2_out), .out_3(onoff_2_out_3));
  OnOff onoff_3 (.A(A), .in_2(and_1_out), .out_3(onoff_3_out_3));
  OnOff onoff_4 (.A(B), .in_2(and_1_out), .out_3(onoff_4_out_3));
  OnOff onoff_5 (.A(A), .in_2(and_3_out), .out_3(onoff_5_out_3));
  OnOff onoff_6 (.A(B), .in_2(and_3_out), .out_3(onoff_6_out_3));
  OnOff onoff_7 (.A(A), .in_2(and_4_out), .out_3(onoff_7_out_3));
  OnOff onoff_8 (.A(B), .in_2(and_4_out), .out_3(onoff_8_out_3));
  AND4bits and4bits_1 (.A(onoff_1_out_3), .in_2(onoff_2_out_3), .S(and4bits_1_s));
  OR4bits or4bits_1 (.A(onoff_3_out_3), .in_2(onoff_4_out_3), .S(or4bits_1_s));
  sumador_flags sumador_flags_1 (
    .A(onoff_5_out_3), .B(inversor_4_1_s), .S(sumador_flags_1_s), .V(sumador_flags_1_v), .C(sumador_flags_1_c));  // open: Cin, N, Z
  inversor_4 inversor_4_1 (.A(onoff_6_out_3), .INV(and_3_out), .S(inversor_4_1_s));
  sumador_flags sumador_flags_2 (
    .A(onoff_7_out_3), .B(onoff_8_out_3), .S(sumador_flags_2_s), .V(sumador_flags_2_v), .C(sumador_flags_2_c));  // open: Cin, N, Z
  not not_5 (not_5_out, sumador_flags_1_c);
  and and_5 (and_5_out, not_5_out, and_3_out);
  not not_6 (not_6_out, sumador_flags_2_c);
  and and_6 (and_6_out, not_6_out, and_4_out);
  or or_1 (V, sumador_flags_1_v, sumador_flags_2_v);
  ElejirSalida elejirsalida_1 (
    .A(or4bits_1_s), .B(and4bits_1_s), .C(sumador_flags_1_s), .D(sumador_flags_2_s), .OP(OP), .S({N, S[2:0]}));
  comparador_cero comparador_cero_1 (.A({N, S[2:0]}), .Z(Z));
  or or_2 (C, and_5_out, and_6_out);
  Hex_Digit_Display hex_digit_display_1 (.value({N, S[2:0]}));  // open: dp

  assign S[3] = N;
endmodule

module verificador (
  output [3:0] out_1,
  output [3:0] out_2,
  output [1:0] out_3,
  output halt,
  output N,
  output Z,
  output V,
  output C,
  output [3:0] res
);

  wire clock_1_out;

  Clock clock_1 (.out(clock_1_out));
  Counter #(.max('h3ff), .width(10)) counter_1 (
    .clk(clock_1_out), .carry(halt), .Q({out_3, out_2, out_1}));  // open: clr, load, up, count, D
  ALU alu_1 (.A(out_1), .B(out_2), .OP(out_3), .N(N), .Z(Z), .V(V), .C(C), .S(res));
endmodule

module OnOff (
  input  [3:0] A,
  input  in_2,
  output [3:0] out_3
);

  and and_1 (out_3[0], A[0], in_2);
  and and_2 (out_3[1], A[1], in_2);
  and and_3 (out_3[2], A[2], in_2);
  and and_4 (out_3[3], A[3], in_2);
endmodule

module OR4bits (
  input  [3:0] A,
  input  [3:0] in_2,
  output [3:0] S
);

  or or_1 (S[0], A[0], in_2[0]);
  or or_2 (S[1], A[1], in_2[1]);
  or or_3 (S[2], A[2], in_2[2]);
  or or_4 (S[3], A[3], in_2[3]);
endmodule

module AND4bits (
  input  [3:0] A,
  input  [3:0] in_2,
  output [3:0] S
);

  and and_1 (S[0], A[0], in_2[0]);
  and and_2 (S[1], A[1], in_2[1]);
  and and_3 (S[2], A[2], in_2[2]);
  and and_4 (S[3], A[3], in_2[3]);
endmodule

module ElejirSalida (
  input  [3:0] A,
  input  [3:0] B,
  input  [3:0] C,
  input  [3:0] D,
  input  [1:0] OP,
  output [3:0] S
);

  wire and_1_out, and_2_out, and_3_out, and_4_out, not_1_out, not_2_out, not_3_out, not_4_out;
  wire [3:0] onoff_1_out_3, onoff_2_out_3, onoff_3_out_3, onoff_4_out_3, sumador_4_1_s, sumador_4_2_s;

  not not_1 (not_1_out, OP[0]);
  not not_2 (not_2_out, OP[1]);
  not not_3 (not_3_out, OP[0]);
  not not_4 (not_4_out, OP[1]);
  and and_1 (and_1_out, OP[0], OP[1]);
  and and_2 (and_2_out, not_1_out, OP[1]);
  and and_3 (and_3_out, OP[0], not_2_out);
  and and_4 (and_4_out, not_3_out, not_4_out);
  OnOff onoff_1 (.A(A), .in_2(and_1_out), .out_3(onoff_1_out_3));
  OnOff onoff_2 (.A(B), .in_2(and_2_out), .out_3(onoff_2_out_3));
  OnOff onoff_3 (.A(C), .in_2(and_3_out), .out_3(onoff_3_out_3));
  OnOff onoff_4 (.A(D), .in_2(and_4_out), .out_3(onoff_4_out_3));
  sumador_4 sumador_4_1 (.A(onoff_1_out_3), .B(onoff_2_out_3), .S(sumador_4_1_s));  // open: Cin, Cout
  sumador_4 sumador_4_2 (.A(onoff_3_out_3), .B(onoff_4_out_3), .S(sumador_4_2_s));  // open: Cin, Cout
  sumador_4 sumador_4_3 (.A(sumador_4_1_s), .B(sumador_4_2_s), .S(S));  // open: Cin, Cout
endmodule

module SumFLAGSC2 (
  input  Cin,
  input  [3:0] A,
  input  [3:0] B,
  output [3:0] S,
  output N,
  output Z,
  output V,
  output C
);

  wire and_1_out, and_2_out, and_3_out, and_4_out, not_1_out, not_2_out, not_3_out;
  wire [3:0] sumador_4_1_s;

  not not_1 (not_1_out, A[3]);
  not not_2 (not_2_out, B[3]);
  and and_1 (and_1_out, not_1_out, not_2_out);
  and and_2 (and_2_out, A[3], B[3]);
  sumador_4 sumador_4_1 (.A(A), .Cin(Cin), .B(B), .S(sumador_4_1_s));  // open: Cout
  inversor_4 inversor_4_1 (.A(sumador_4_1_s), .S({N, S[2:0]}));  // open: INV
  not not_3 (not_3_out, N);
  Hex_Digit_Display hex_digit_display_1 (.value({N, S[2:0]}));  // open: dp
  comparador_cero comparador_cero_1 (.A({N, S[2:0]}), .Z(Z));
  and and_3 (and_3_out, N, and_1_out);
  and and_4 (and_4_out, not_3_out, and_2_out);
  or or_1 (V, and_3_out, and_4_out);

  assign S[3] = N;
endmodule
